// Logisim project 8bit_CPU.circ as structural Verilog: 30 circuits, main circuit main
module main (
  input  in_1,
  input  in_2,
  input  in_3,
  input  in_4,
  input  in_5,
  input  [7:0] in_6,
  output [7:0] out_7,
  output [7:0] out_8,
  output [7:0] out_9,
  output [7:0] out_10
);

  wire clock_1_out, cpu_alu_1_out_7, cpu_alu_1_out_8, cpu_alu_1_out_9, cpu_alu_1_out_11, cpu_clock_1_out_2,
       cpu_clock_1_out_3, cpu_clock_1_out_4, cpu_control_unit_1_acc_e, cpu_control_unit_1_acc_s,
       cpu_control_unit_1_iar_e, cpu_control_unit_1_ir_s, cpu_control_unit_1_mar_s, cpu_control_unit_1_out_6,
       cpu_control_unit_1_r0_e, cpu_control_unit_1_r0_s, cpu_control_unit_1_r1_e, cpu_control_unit_1_r1_s,
       cpu_control_unit_1_r2_e, cpu_control_unit_1_r2_s, cpu_control_unit_1_r3_e, cpu_control_unit_1_r3_s,
       cpu_control_unit_1_ram_e, cpu_control_unit_1_ram_s, cpu_control_unit_1_tmp_s, cpu_flags_1_out_6,
       cpu_flags_1_out_7, cpu_flags_1_out_8, cpu_flags_1_out_9;
  wire [7:0] cpu_alu_1_out_10, cpu_bus_1_1_out_3, cpu_r_accum_1_out_4, cpu_r_ir_1_out_3, cpu_r_tmp_1_out_3;

  cpu_alu cpu_alu_1 (
    .out_7(cpu_alu_1_out_7), .out_8(cpu_alu_1_out_8), .out_10(cpu_alu_1_out_10), .out_11(cpu_alu_1_out_11),
    .out_9(cpu_alu_1_out_9), .in_1(cpu_r_accum_1_out_4), .in_2(cpu_bus_1_1_out_3), .in_3(cpu_flags_1_out_6),
    .in_4(in_3), .in_5(in_2), .in_6(in_1));
  cpu_r_tmp cpu_r_tmp_1 (.out_3(cpu_r_tmp_1_out_3), .in_1(cpu_r_accum_1_out_4), .in_2(cpu_control_unit_1_tmp_s));
  cpu_bus_1 cpu_bus_1_1 (.out_3(cpu_bus_1_1_out_3), .in_1(cpu_r_tmp_1_out_3), .in_2(cpu_control_unit_1_out_6));
  cpu_r_accum cpu_r_accum_1 (
    .out_4(cpu_r_accum_1_out_4), .in_1(cpu_alu_1_out_10), .in_2(cpu_control_unit_1_acc_s),
    .in_3(cpu_control_unit_1_acc_e));
  Clock clock_1 (.out(clock_1_out));
  cpu_flags cpu_flags_1 (
    .out_6(cpu_flags_1_out_6), .out_7(cpu_flags_1_out_7), .out_8(cpu_flags_1_out_8),
    .out_9(cpu_flags_1_out_9), .in_1(cpu_alu_1_out_11), .in_2(cpu_alu_1_out_7), .in_3(cpu_alu_1_out_8),
    .in_4(cpu_alu_1_out_9), .in_5(1'b1));
  cpu_clock cpu_clock_1 (
    .out_2(cpu_clock_1_out_2), .out_3(cpu_clock_1_out_3), .out_4(cpu_clock_1_out_4), .in_1(clock_1_out));
  cpu_r cpu_r_1 (
    .out_5(out_10), .out_4(cpu_r_accum_1_out_4), .in_1(cpu_r_accum_1_out_4), .in_2(cpu_control_unit_1_r0_s),
    .in_3(cpu_control_unit_1_r0_e));
  cpu_r cpu_r_2 (
    .out_5(out_7), .out_4(cpu_r_accum_1_out_4), .in_1(cpu_r_accum_1_out_4), .in_2(cpu_control_unit_1_r1_s),
    .in_3(cpu_control_unit_1_r1_e));
  cpu_r_iar cpu_r_iar_1 (
    .out_4(cpu_r_accum_1_out_4), .in_1(cpu_r_accum_1_out_4), .in_2(1'b1), .in_3(cpu_control_unit_1_iar_e));
  cpu_r cpu_r_3 (
    .out_5(out_8), .out_4(cpu_r_accum_1_out_4), .in_1(cpu_r_accum_1_out_4), .in_2(cpu_control_unit_1_r2_s),
    .in_3(cpu_control_unit_1_r2_e));
  cpu_r_ir cpu_r_ir_1 (.out_3(cpu_r_ir_1_out_3), .in_1(cpu_r_accum_1_out_4), .in_2(cpu_control_unit_1_ir_s));
  cpu_r cpu_r_4 (
    .out_5(out_9), .out_4(cpu_r_accum_1_out_4), .in_1(cpu_r_accum_1_out_4), .in_2(cpu_control_unit_1_r3_s),
    .in_3(cpu_control_unit_1_r3_e));
  cpu_control_unit cpu_control_unit_1 (
    .MAR_S(cpu_control_unit_1_mar_s), .ACC_S(cpu_control_unit_1_acc_s), .RAM_S(cpu_control_unit_1_ram_s),
    .TMP_S(cpu_control_unit_1_tmp_s), .R0_S(cpu_control_unit_1_r0_s), .R1_S(cpu_control_unit_1_r1_s),
    .R2_S(cpu_control_unit_1_r2_s), .R3_S(cpu_control_unit_1_r3_s), .IR_S(cpu_control_unit_1_ir_s),
    .RAM_E(cpu_control_unit_1_ram_e), .ACC_E(cpu_control_unit_1_acc_e), .IAR_E(cpu_control_unit_1_iar_e),
    .R0_E(cpu_control_unit_1_r0_e), .R1_E(cpu_control_unit_1_r1_e), .R2_E(cpu_control_unit_1_r2_e),
    .R3_E(cpu_control_unit_1_r3_e), .out_6(cpu_control_unit_1_out_6), .clks(cpu_clock_1_out_3),
    .clk(cpu_clock_1_out_2), .clke(cpu_clock_1_out_4), .IR_IN(cpu_r_ir_1_out_3), .Refresh(in_4));  // open: IAR_S
  cpu_ram_256 cpu_ram_256_1 (
    .out_7(cpu_r_accum_1_out_4), .in_5(cpu_control_unit_1_ram_s), .in_6(cpu_control_unit_1_ram_e),
    .in_1(in_5), .in_2(in_6), .in_3(cpu_r_accum_1_out_4), .in_4(cpu_control_unit_1_mar_s));
endmodule

// 1bitM
module cpu_1bit_mem (
  input  in_1,
  input  in_2,
  output out_3
);

  wire nand_1_out, nand_2_out, nand_4_out;

  nand nand_1 (nand_1_out, in_1, in_2);
  nand nand_2 (nand_2_out, nand_1_out, in_2);
  nand nand_3 (out_3, nand_1_out, nand_4_out);
  nand nand_4 (nand_4_out, out_3, nand_2_out);
endmodule

// 8bitM
module cpu_8bit_mem (
  input  [7:0] in_1,
  input  in_2,
  output [7:0] out_3
);

  cpu_1bit_mem cpu_1bit_mem_1 (.in_1(in_1[0]), .in_2(in_2), .out_3(out_3[0]));
  cpu_1bit_mem cpu_1bit_mem_2 (.in_1(in_1[1]), .in_2(in_2), .out_3(out_3[1]));
  cpu_1bit_mem cpu_1bit_mem_3 (.in_1(in_1[2]), .in_2(in_2), .out_3(out_3[2]));
  cpu_1bit_mem cpu_1bit_mem_4 (.in_1(in_1[3]), .in_2(in_2), .out_3(out_3[3]));
  cpu_1bit_mem cpu_1bit_mem_5 (.in_1(in_1[4]), .in_2(in_2), .out_3(out_3[4]));
  cpu_1bit_mem cpu_1bit_mem_6 (.in_1(in_1[5]), .in_2(in_2), .out_3(out_3[5]));
  cpu_1bit_mem cpu_1bit_mem_7 (.in_1(in_1[6]), .in_2(in_2), .out_3(out_3[6]));
  cpu_1bit_mem cpu_1bit_mem_8 (.in_1(in_1[7]), .in_2(in_2), .out_3(out_3[7]));
endmodule

module cpu_enable_8 (
  input  [7:0] in_1,
  input  in_2,
  output [7:0] out_3
);

  wire and_1_out, and_2_out, and_3_out, and_4_out, and_5_out, and_6_out, and_7_out, and_8_out;

  and and_1 (and_1_out, in_1[0], in_2);
  and and_2 (and_2_out, in_1[1], in_2);
  and and_3 (and_3_out, in_1[2], in_2);
  and and_4 (and_4_out, in_1[3], in_2);
  and and_5 (and_5_out, in_1[4], in_2);
  and and_6 (and_6_out, in_1[5], in_2);
  and and_7 (and_7_out, in_1[6], in_2);
  and and_8 (and_8_out, in_1[7], in_2);
  assign out_3[0] = in_2 ? and_1_out : 1'bz;  // Controlled_Buffer controlled_buffer_1
  assign out_3[1] = in_2 ? and_2_out : 1'bz;  // Controlled_Buffer controlled_buffer_2
  assign out_3[2] = in_2 ? and_3_out : 1'bz;  // Controlled_Buffer controlled_buffer_3
  assign out_3[3] = in_2 ? and_4_out : 1'bz;  // Controlled_Buffer controlled_buffer_4
  assign out_3[4] = in_2 ? and_5_out : 1'bz;  // Controlled_Buffer controlled_buffer_5
  assign out_3[5] = in_2 ? and_6_out : 1'bz;  // Controlled_Buffer controlled_buffer_6
  assign out_3[6] = in_2 ? and_7_out : 1'bz;  // Controlled_Buffer controlled_buffer_7
  assign out_3[7] = in_2 ? and_8_out : 1'bz;  // Controlled_Buffer controlled_buffer_8
endmodule

module cpu_reg_8 (
  input  [7:0] in_1,
  input  in_2,
  input  in_3,
  output [7:0] out_4,
  output [7:0] out_5
);

  wire [7:0] cpu_enable_8_1_out_3;

  cpu_8bit_mem cpu_8bit_mem_1 (.out_3(out_4), .in_1(in_1), .in_2(in_2));
  cpu_enable_8 cpu_enable_8_1 (.out_3(cpu_enable_8_1_out_3), .in_1(out_4), .in_2(in_3));
  assign out_5 = in_3 ? cpu_enable_8_1_out_3 : 8'bz;  // Controlled_Buffer controlled_buffer_1
endmodule

module cpu_dec_4x16 (
  input  [3:0] in_1,
  output out_2,
  output out_3,
  output out_4,
  output out_5,
  output out_6,
  output out_7,
  output out_8,
  output out_9,
  output out_10,
  output out_11,
  output out_12,
  output out_13,
  output out_14,
  output out_15,
  output out_16,
  output out_17
);

  wire not_1_out, not_2_out, not_3_out, not_4_out;

  not not_1 (not_1_out, in_1[3]);
  not not_2 (not_2_out, in_1[1]);
  not not_3 (not_3_out, in_1[2]);
  not not_4 (not_4_out, in_1[0]);
  and and_1 (out_2, not_4_out, not_2_out, not_3_out, not_1_out);
  and and_2 (out_3, in_1[0], not_2_out, not_3_out, not_1_out);
  and and_3 (out_4, not_4_out, in_1[1], not_3_out, not_1_out);
  and and_4 (out_5, in_1[0], in_1[1], not_3_out, not_1_out);
  and and_5 (out_6, not_4_out, not_2_out, in_1[2], not_1_out);
  and and_6 (out_7, in_1[0], not_2_out, in_1[2], not_1_out);
  and and_7 (out_8, not_4_out, in_1[1], in_1[2], not_1_out);
  and and_8 (out_9, in_1[0], in_1[1], in_1[2], not_1_out);
  and and_9 (out_10, not_4_out, not_2_out, not_3_out, in_1[3]);
  and and_10 (out_11, in_1[0], not_2_out, not_3_out, in_1[3]);
  and and_11 (out_12, not_4_out, in_1[1], not_3_out, in_1[3]);
  and and_12 (out_13, in_1[0], in_1[1], not_3_out, in_1[3]);
  and and_13 (out_14, not_4_out, not_2_out, in_1[2], in_1[3]);
  and and_14 (out_15, in_1[0], not_2_out, in_1[2], in_1[3]);
  and and_15 (out_16, not_4_out, in_1[1], in_1[2], in_1[3]);
  and and_16 (out_17, in_1[0], in_1[1], in_1[2], in_1[3]);
endmodule

module cpu_reg_byte (
  input  [7:0] in_1,
  input  in_2,
  input  in_3,
  input  in_4,
  input  in_5,
  input  in_6,
  output [7:0] out_7,
  output [7:0] out_8
);

  wire and_1_out, and_2_out, and_3_out, or_1_out;
  wire [7:0] cpu_reg_8_1_out_5;

  and and_1 (and_1_out, in_3, in_4);
  and and_2 (and_2_out, and_1_out, in_5);
  and and_3 (and_3_out, and_1_out, in_6);
  or or_1 (or_1_out, in_2, and_2_out);
  cpu_reg_8 cpu_reg_8_1 (.out_4(out_7), .out_5(cpu_reg_8_1_out_5), .in_1(in_1), .in_2(or_1_out), .in_3(and_3_out));
  assign out_8 = and_3_out ? cpu_reg_8_1_out_5 : 8'bz;  // Controlled_Buffer controlled_buffer_1
endmodule

module cpu_ram_256 (
  input  in_1,
  input  [7:0] in_2,
  input  [7:0] in_3,
  input  in_4,
  input  in_5,
  input  in_6,
  output [7:0] out_7
);

  wire cpu_dec_4x16_1_out_2, cpu_dec_4x16_1_out_3, cpu_dec_4x16_1_out_4, cpu_dec_4x16_1_out_5,
       cpu_dec_4x16_1_out_6, cpu_dec_4x16_1_out_7, cpu_dec_4x16_1_out_8, cpu_dec_4x16_1_out_9,
       cpu_dec_4x16_1_out_10, cpu_dec_4x16_1_out_11, cpu_dec_4x16_1_out_12, cpu_dec_4x16_1_out_13,
       cpu_dec_4x16_1_out_14, cpu_dec_4x16_1_out_15, cpu_dec_4x16_1_out_16, cpu_dec_4x16_1_out_17,
       cpu_dec_4x16_2_out_2, cpu_dec_4x16_2_out_3, cpu_dec_4x16_2_out_4, cpu_dec_4x16_2_out_5,
       cpu_dec_4x16_2_out_6, cpu_dec_4x16_2_out_7, cpu_dec_4x16_2_out_8, cpu_dec_4x16_2_out_9,
       cpu_dec_4x16_2_out_10, cpu_dec_4x16_2_out_11, cpu_dec_4x16_2_out_12, cpu_dec_4x16_2_out_13,
       cpu_dec_4x16_2_out_14, cpu_dec_4x16_2_out_15, cpu_dec_4x16_2_out_16, cpu_dec_4x16_2_out_17;
  wire [7:0] cpu_8bit_mem_1_out_3, cpu_reg_byte_1_out_8;

  assign out_7 = in_6 ? cpu_reg_byte_1_out_8 : 8'bz;  // Controlled_Buffer controlled_buffer_1
  cpu_8bit_mem cpu_8bit_mem_1 (.out_3(cpu_8bit_mem_1_out_3), .in_1(in_3), .in_2(in_4));
  cpu_dec_4x16 cpu_dec_4x16_1 (
    .out_3(cpu_dec_4x16_1_out_3), .out_4(cpu_dec_4x16_1_out_4), .out_5(cpu_dec_4x16_1_out_5),
    .out_6(cpu_dec_4x16_1_out_6), .out_7(cpu_dec_4x16_1_out_7), .out_8(cpu_dec_4x16_1_out_8),
    .out_9(cpu_dec_4x16_1_out_9), .out_10(cpu_dec_4x16_1_out_10), .out_11(cpu_dec_4x16_1_out_11),
    .out_12(cpu_dec_4x16_1_out_12), .out_2(cpu_dec_4x16_1_out_2), .out_13(cpu_dec_4x16_1_out_13),
    .out_14(cpu_dec_4x16_1_out_14), .out_15(cpu_dec_4x16_1_out_15), .out_16(cpu_dec_4x16_1_out_16),
    .out_17(cpu_dec_4x16_1_out_17), .in_1(cpu_8bit_mem_1_out_3[7:4]));
  cpu_reg_byte cpu_reg_byte_1 (
    .out_8(cpu_reg_byte_1_out_8), .in_6(in_6), .in_2(in_1), .in_1(in_2), .in_3(cpu_dec_4x16_1_out_2),
    .in_4(cpu_dec_4x16_2_out_17), .in_5(in_5));  // open: out_7
  cpu_reg_byte cpu_reg_byte_2 (
    .out_8(cpu_reg_byte_1_out_8), .in_6(in_6), .in_2(in_1), .in_1(in_2), .in_3(cpu_dec_4x16_1_out_3),
    .in_4(cpu_dec_4x16_2_out_17), .in_5(in_5));  // open: out_7
  cpu_reg_byte cpu_reg_byte_3 ();  // open: out_7, out_8, in_6, in_2, in_1, in_3, in_4, in_5
  cpu_reg_byte cpu_reg_byte_4 ();  // open: out_7, out_8, in_6, in_2, in_1, in_3, in_4, in_5
  cpu_reg_byte cpu_reg_byte_5 ();  // open: out_7, out_8, in_6, in_2, in_1, in_3, in_4, in_5
  cpu_reg_byte cpu_reg_byte_6 (
    .out_8(cpu_reg_byte_1_out_8), .in_6(in_6), .in_2(in_1), .in_1(in_2), .in_3(cpu_dec_4x16_1_out_2),
    .in_4(cpu_dec_4x16_2_out_16), .in_5(in_5));  // open: out_7
  cpu_reg_byte cpu_reg_byte_7 (
    .out_8(cpu_reg_byte_1_out_8), .in_6(in_6), .in_2(in_1), .in_1(in_2), .in_3(cpu_dec_4x16_1_out_3),
    .in_4(cpu_dec_4x16_2_out_16), .in_5(in_5));  // open: out_7
  cpu_reg_byte cpu_reg_byte_8 ();  // open: out_7, out_8, in_6, in_2, in_1, in_3, in_4, in_5
  cpu_reg_byte cpu_reg_byte_9 ();  // open: out_7, out_8, in_6, in_2, in_1, in_3, in_4, in_5
  cpu_reg_byte cpu_reg_byte_10 ();  // open: out_7, out_8, in_6, in_2, in_1, in_3, in_4, in_5
  cpu_reg_byte cpu_reg_byte_11 (
    .out_8(cpu_reg_byte_1_out_8), .in_6(in_6), .in_2(in_1), .in_1(in_2), .in_3(cpu_dec_4x16_1_out_2),
    .in_4(cpu_dec_4x16_2_out_15), .in_5(in_5));  // open: out_7
  cpu_reg_byte cpu_reg_byte_12 (
    .out_8(cpu_reg_byte_1_out_8), .in_6(in_6), .in_2(in_1), .in_1(in_2), .in_3(cpu_dec_4x16_1_out_3),
    .in_4(cpu_dec_4x16_2_out_15), .in_5(in_5));  // open: out_7
  cpu_reg_byte cpu_reg_byte_13 ();  // open: out_7, out_8, in_6, in_2, in_1, in_3, in_4, in_5
  cpu_reg_byte cpu_reg_byte_14 ();  // open: out_7, out_8, in_6, in_2, in_1, in_3, in_4, in_5
  cpu_reg_byte cpu_reg_byte_15 ();  // open: out_7, out_8, in_6, in_2, in_1, in_3, in_4, in_5
  cpu_reg_byte cpu_reg_byte_16 (
    .out_8(cpu_reg_byte_1_out_8), .in_6(in_6), .in_2(in_1), .in_1(in_2), .in_3(cpu_dec_4x16_1_out_2),
    .in_4(cpu_dec_4x16_2_out_14), .in_5(in_5));  // open: out_7
  cpu_reg_byte cpu_reg_byte_17 (
    .out_8(cpu_reg_byte_1_out_8), .in_6(in_6), .in_2(in_1), .in_1(in_2), .in_3(cpu_dec_4x16_1_out_3),
    .in_4(cpu_dec_4x16_2_out_14), .in_5(in_5));  // open: out_7
  cpu_reg_byte cpu_reg_byte_18 ();  // open: out_7, out_8, in_6, in_2, in_1, in_3, in_4, in_5
  cpu_reg_byte cpu_reg_byte_19 ();  // open: out_7, out_8, in_6, in_2, in_1, in_3, in_4, in_5
  cpu_reg_byte cpu_reg_byte_20 ();  // open: out_7, out_8, in_6, in_2, in_1, in_3, in_4, in_5
  cpu_reg_byte cpu_reg_byte_21 (
    .out_8(cpu_reg_byte_1_out_8), .in_6(in_6), .in_2(in_1), .in_1(in_2), .in_3(cpu_dec_4x16_1_out_2),
    .in_4(cpu_dec_4x16_2_out_13), .in_5(in_5));  // open: out_7
  cpu_reg_byte cpu_reg_byte_22 (
    .out_8(cpu_reg_byte_1_out_8), .in_6(in_6), .in_2(in_1), .in_1(in_2), .in_3(cpu_dec_4x16_1_out_3),
    .in_4(cpu_dec_4x16_2_out_13), .in_5(in_5));  // open: out_7
  cpu_reg_byte cpu_reg_byte_23 ();  // open: out_7, out_8, in_6, in_2, in_1, in_3, in_4, in_5
  cpu_reg_byte cpu_reg_byte_24 ();  // open: out_7, out_8, in_6, in_2, in_1, in_3, in_4, in_5
  cpu_reg_byte cpu_reg_byte_25 ();  // open: out_7, out_8, in_6, in_2, in_1, in_3, in_4, in_5
  cpu_reg_byte cpu_reg_byte_26 (
    .out_8(cpu_reg_byte_1_out_8), .in_6(in_6), .in_2(in_1), .in_1(in_2), .in_3(cpu_dec_4x16_1_out_2),
    .in_4(cpu_dec_4x16_2_out_12), .in_5(in_5));  // open: out_7
  cpu_reg_byte cpu_reg_byte_27 (
    .out_8(cpu_reg_byte_1_out_8), .in_6(in_6), .in_2(in_1), .in_1(in_2), .in_3(cpu_dec_4x16_1_out_3),
    .in_4(cpu_dec_4x16_2_out_12), .in_5(in_5));  // open: out_7
  cpu_reg_byte cpu_reg_byte_28 ();  // open: out_7, out_8, in_6, in_2, in_1, in_3, in_4, in_5
  cpu_reg_byte cpu_reg_byte_29 ();  // open: out_7, out_8, in_6, in_2, in_1, in_3, in_4, in_5
  cpu_reg_byte cpu_reg_byte_30 ();  // open: out_7, out_8, in_6, in_2, in_1, in_3, in_4, in_5
  cpu_reg_byte cpu_reg_byte_31 (
    .out_8(cpu_reg_byte_1_out_8), .in_6(in_6), .in_2(in_1), .in_1(in_2), .in_3(cpu_dec_4x16_1_out_2),
    .in_4(cpu_dec_4x16_2_out_11), .in_5(in_5));  // open: out_7
  cpu_reg_byte cpu_reg_byte_32 (
    .out_8(cpu_reg_byte_1_out_8), .in_6(in_6), .in_2(in_1), .in_1(in_2), .in_3(cpu_dec_4x16_1_out_3),
    .in_4(cpu_dec_4x16_2_out_11), .in_5(in_5));  // open: out_7
  cpu_reg_byte cpu_reg_byte_33 ();  // open: out_7, out_8, in_6, in_2, in_1, in_3, in_4, in_5
  cpu_reg_byte cpu_reg_byte_34 ();  // open: out_7, out_8, in_6, in_2, in_1, in_3, in_4, in_5
  cpu_reg_byte cpu_reg_byte_35 ();  // open: out_7, out_8, in_6, in_2, in_1, in_3, in_4, in_5
  cpu_dec_4x16 cpu_dec_4x16_2 (
    .out_3(cpu_dec_4x16_2_out_3), .out_4(cpu_dec_4x16_2_out_4), .out_5(cpu_dec_4x16_2_out_5),
    .out_6(cpu_dec_4x16_2_out_6), .out_7(cpu_dec_4x16_2_out_7), .out_8(cpu_dec_4x16_2_out_8),
    .out_9(cpu_dec_4x16_2_out_9), .out_10(cpu_dec_4x16_2_out_10), .out_11(cpu_dec_4x16_2_out_11),
    .out_12(cpu_dec_4x16_2_out_12), .out_2(cpu_dec_4x16_2_out_2), .out_13(cpu_dec_4x16_2_out_13),
    .out_14(cpu_dec_4x16_2_out_14), .out_15(cpu_dec_4x16_2_out_15), .out_16(cpu_dec_4x16_2_out_16),
    .out_17(cpu_dec_4x16_2_out_17), .in_1(cpu_8bit_mem_1_out_3[3:0]));
  cpu_reg_byte cpu_reg_byte_36 (
    .out_8(cpu_reg_byte_1_out_8), .in_6(in_6), .in_2(in_1), .in_1(in_2), .in_3(cpu_dec_4x16_1_out_2),
    .in_4(cpu_dec_4x16_2_out_10), .in_5(in_5));  // open: out_7
  cpu_reg_byte cpu_reg_byte_37 (
    .out_8(cpu_reg_byte_1_out_8), .in_6(in_6), .in_2(in_1), .in_1(in_2), .in_3(cpu_dec_4x16_1_out_3),
    .in_4(cpu_dec_4x16_2_out_10), .in_5(in_5));  // open: out_7
  cpu_reg_byte cpu_reg_byte_38 ();  // open: out_7, out_8, in_6, in_2, in_1, in_3, in_4, in_5
  cpu_reg_byte cpu_reg_byte_39 ();  // open: out_7, out_8, in_6, in_2, in_1, in_3, in_4, in_5
  cpu_reg_byte cpu_reg_byte_40 ();  // open: out_7, out_8, in_6, in_2, in_1, in_3, in_4, in_5
  cpu_reg_byte cpu_reg_byte_41 (
    .out_8(cpu_reg_byte_1_out_8), .in_6(in_6), .in_2(in_1), .in_1(in_2), .in_3(cpu_dec_4x16_1_out_2),
    .in_4(cpu_dec_4x16_2_out_9), .in_5(in_5));  // open: out_7
  cpu_reg_byte cpu_reg_byte_42 (
    .out_8(cpu_reg_byte_1_out_8), .in_6(in_6), .in_2(in_1), .in_1(in_2), .in_3(cpu_dec_4x16_1_out_3),
    .in_4(cpu_dec_4x16_2_out_9), .in_5(in_5));  // open: out_7
  cpu_reg_byte cpu_reg_byte_43 ();  // open: out_7, out_8, in_6, in_2, in_1, in_3, in_4, in_5
  cpu_reg_byte cpu_reg_byte_44 ();  // open: out_7, out_8, in_6, in_2, in_1, in_3, in_4, in_5
  cpu_reg_byte cpu_reg_byte_45 ();  // open: out_7, out_8, in_6, in_2, in_1, in_3, in_4, in_5
  cpu_reg_byte cpu_reg_byte_46 (
    .out_8(cpu_reg_byte_1_out_8), .in_6(in_6), .in_2(in_1), .in_1(in_2), .in_3(cpu_dec_4x16_1_out_2),
    .in_4(cpu_dec_4x16_2_out_8), .in_5(in_5));  // open: out_7
  cpu_reg_byte cpu_reg_byte_47 (
    .out_8(cpu_reg_byte_1_out_8), .in_6(in_6), .in_2(in_1), .in_1(in_2), .in_3(cpu_dec_4x16_1_out_3),
    .in_4(cpu_dec_4x16_2_out_8), .in_5(in_5));  // open: out_7
  cpu_reg_byte cpu_reg_byte_48 ();  // open: out_7, out_8, in_6, in_2, in_1, in_3, in_4, in_5
  cpu_reg_byte cpu_reg_byte_49 ();  // open: out_7, out_8, in_6, in_2, in_1, in_3, in_4, in_5
  cpu_reg_byte cpu_reg_byte_50 ();  // open: out_7, out_8, in_6, in_2, in_1, in_3, in_4, in_5
  cpu_reg_byte cpu_reg_byte_51 (
    .out_8(cpu_reg_byte_1_out_8), .in_6(in_6), .in_2(in_1), .in_1(in_2), .in_3(cpu_dec_4x16_1_out_2),
    .in_4(cpu_dec_4x16_2_out_7), .in_5(in_5));  // open: out_7
  cpu_reg_byte cpu_reg_byte_52 (
    .out_8(cpu_reg_byte_1_out_8), .in_6(in_6), .in_2(in_1), .in_1(in_2), .in_3(cpu_dec_4x16_1_out_3),
    .in_4(cpu_dec_4x16_2_out_7), .in_5(in_5));  // open: out_7
  cpu_reg_byte cpu_reg_byte_53 ();  // open: out_7, out_8, in_6, in_2, in_1, in_3, in_4, in_5
  cpu_reg_byte cpu_reg_byte_54 ();  // open: out_7, out_8, in_6, in_2, in_1, in_3, in_4, in_5
  cpu_reg_byte cpu_reg_byte_55 ();  // open: out_7, out_8, in_6, in_2, in_1, in_3, in_4, in_5
  cpu_reg_byte cpu_reg_byte_56 (
    .out_8(cpu_reg_byte_1_out_8), .in_6(in_6), .in_2(in_1), .in_1(in_2), .in_3(cpu_dec_4x16_1_out_2),
    .in_4(cpu_dec_4x16_2_out_6), .in_5(in_5));  // open: out_7
  cpu_reg_byte cpu_reg_byte_57 (
    .out_8(cpu_reg_byte_1_out_8), .in_6(in_6), .in_2(in_1), .in_1(in_2), .in_3(cpu_dec_4x16_1_out_3),
    .in_4(cpu_dec_4x16_2_out_6), .in_5(in_5));  // open: out_7
  cpu_reg_byte cpu_reg_byte_58 ();  // open: out_7, out_8, in_6, in_2, in_1, in_3, in_4, in_5
  cpu_reg_byte cpu_reg_byte_59 ();  // open: out_7, out_8, in_6, in_2, in_1, in_3, in_4, in_5
  cpu_reg_byte cpu_reg_byte_60 ();  // open: out_7, out_8, in_6, in_2, in_1, in_3, in_4, in_5
  cpu_reg_byte cpu_reg_byte_61 (
    .out_8(cpu_reg_byte_1_out_8), .in_6(in_6), .in_2(in_1), .in_1(in_2), .in_3(cpu_dec_4x16_1_out_2),
    .in_4(cpu_dec_4x16_2_out_5), .in_5(in_5));  // open: out_7
  cpu_reg_byte cpu_reg_byte_62 (
    .out_8(cpu_reg_byte_1_out_8), .in_6(in_6), .in_2(in_1), .in_1(in_2), .in_3(cpu_dec_4x16_1_out_3),
    .in_4(cpu_dec_4x16_2_out_5), .in_5(in_5));  // open: out_7
  cpu_reg_byte cpu_reg_byte_63 ();  // open: out_7, out_8, in_6, in_2, in_1, in_3, in_4, in_5
  cpu_reg_byte cpu_reg_byte_64 ();  // open: out_7, out_8, in_6, in_2, in_1, in_3, in_4, in_5
  cpu_reg_byte cpu_reg_byte_65 ();  // open: out_7, out_8, in_6, in_2, in_1, in_3, in_4, in_5
  cpu_reg_byte cpu_reg_byte_66 (
    .out_8(cpu_reg_byte_1_out_8), .in_6(in_6), .in_2(in_1), .in_1(in_2), .in_3(cpu_dec_4x16_1_out_2),
    .in_4(cpu_dec_4x16_2_out_4), .in_5(in_5));  // open: out_7
  cpu_reg_byte cpu_reg_byte_67 (
    .out_8(cpu_reg_byte_1_out_8), .in_6(in_6), .in_2(in_1), .in_1(in_2), .in_3(cpu_dec_4x16_1_out_3),
    .in_4(cpu_dec_4x16_2_out_4), .in_5(in_5));  // open: out_7
  cpu_reg_byte cpu_reg_byte_68 ();  // open: out_7, out_8, in_6, in_2, in_1, in_3, in_4, in_5
  cpu_reg_byte cpu_reg_byte_69 ();  // open: out_7, out_8, in_6, in_2, in_1, in_3, in_4, in_5
  cpu_reg_byte cpu_reg_byte_70 ();  // open: out_7, out_8, in_6, in_2, in_1, in_3, in_4, in_5
  cpu_reg_byte cpu_reg_byte_71 (
    .out_8(cpu_reg_byte_1_out_8), .in_6(in_6), .in_2(in_1), .in_1(in_2), .in_3(cpu_dec_4x16_1_out_2),
    .in_4(cpu_dec_4x16_2_out_3), .in_5(in_5));  // open: out_7
  cpu_reg_byte cpu_reg_byte_72 (
    .out_8(cpu_reg_byte_1_out_8), .in_6(in_6), .in_2(in_1), .in_1(in_2), .in_3(cpu_dec_4x16_1_out_3),
    .in_4(cpu_dec_4x16_2_out_3), .in_5(in_5));  // open: out_7
  cpu_reg_byte cpu_reg_byte_73 ();  // open: out_7, out_8, in_6, in_2, in_1, in_3, in_4, in_5
  cpu_reg_byte cpu_reg_byte_74 ();  // open: out_7, out_8, in_6, in_2, in_1, in_3, in_4, in_5
  cpu_reg_byte cpu_reg_byte_75 ();  // open: out_7, out_8, in_6, in_2, in_1, in_3, in_4, in_5
  cpu_reg_byte cpu_reg_byte_76 (
    .out_8(cpu_reg_byte_1_out_8), .in_6(in_6), .in_2(in_1), .in_1(in_2), .in_3(cpu_dec_4x16_1_out_2),
    .in_4(cpu_dec_4x16_2_out_2), .in_5(in_5));  // open: out_7
  cpu_reg_byte cpu_reg_byte_77 (
    .out_8(cpu_reg_byte_1_out_8), .in_6(in_6), .in_2(in_1), .in_1(in_2), .in_3(cpu_dec_4x16_1_out_3),
    .in_4(cpu_dec_4x16_2_out_2), .in_5(in_5));  // open: out_7
  cpu_reg_byte cpu_reg_byte_78 ();  // open: out_7, out_8, in_6, in_2, in_1, in_3, in_4, in_5
  cpu_reg_byte cpu_reg_byte_79 ();  // open: out_7, out_8, in_6, in_2, in_1, in_3, in_4, in_5
  cpu_reg_byte cpu_reg_byte_80 ();  // open: out_7, out_8, in_6, in_2, in_1, in_3, in_4, in_5
endmodule

module cpu_3x8_dec (
  input  in_1,
  input  in_2,
  input  in_3,
  output out_4,
  output out_5,
  output out_6,
  output out_7,
  output out_8,
  output out_9,
  output out_10,
  output out_11
);

  wire not_1_out, not_2_out, not_3_out;

  not not_1 (not_1_out, in_1);
  not not_2 (not_2_out, in_2);
  not not_3 (not_3_out, in_3);
  and and_1 (out_4, not_1_out, not_2_out, not_3_out);
  and and_2 (out_5, in_1, not_2_out, not_3_out);
  and and_3 (out_6, not_1_out, in_2, not_3_out);
  and and_4 (out_7, in_1, in_2, not_3_out);
  and and_5 (out_8, not_1_out, not_2_out, in_3);
  and and_6 (out_9, in_1, not_2_out, in_3);
  and and_7 (out_10, not_1_out, in_2, in_3);
  and and_8 (out_11, in_1, in_2, in_3);
endmodule

module cpu_adder (
  input  in_1,
  input  in_2,
  input  in_3,
  output out_4,
  output out_5
);

  wire and_1_out, and_2_out, xor_1_out;

  xor xor_1 (xor_1_out, in_1, in_2);
  and and_1 (and_1_out, in_3, xor_1_out);
  and and_2 (and_2_out, in_1, in_2);
  xor xor_2 (out_4, xor_1_out, in_3);
  or or_1 (out_5, and_1_out, and_2_out);
endmodule

module cpu_adder_8 (
  input  [7:0] in_1,
  input  [7:0] in_2,
  input  in_3,
  output out_4,
  output [7:0] out_5
);

  wire cpu_adder_2_out_5, cpu_adder_3_out_5, cpu_adder_4_out_5, cpu_adder_5_out_5, cpu_adder_6_out_5,
       cpu_adder_7_out_5, cpu_adder_8_out_5;

  cpu_adder cpu_adder_1 (.out_5(out_4), .out_4(out_5[7]), .in_2(in_2[7]), .in_3(cpu_adder_2_out_5), .in_1(in_1[7]));
  cpu_adder cpu_adder_2 (
    .out_5(cpu_adder_2_out_5), .out_4(out_5[6]), .in_2(in_2[6]), .in_3(cpu_adder_3_out_5), .in_1(in_1[6]));
  cpu_adder cpu_adder_3 (
    .out_5(cpu_adder_3_out_5), .out_4(out_5[5]), .in_2(in_2[5]), .in_3(cpu_adder_4_out_5), .in_1(in_1[5]));
  cpu_adder cpu_adder_4 (
    .out_5(cpu_adder_4_out_5), .out_4(out_5[4]), .in_2(in_2[4]), .in_3(cpu_adder_5_out_5), .in_1(in_1[4]));
  cpu_adder cpu_adder_5 (
    .out_5(cpu_adder_5_out_5), .out_4(out_5[3]), .in_2(in_2[3]), .in_3(cpu_adder_6_out_5), .in_1(in_1[3]));
  cpu_adder cpu_adder_6 (
    .out_5(cpu_adder_6_out_5), .out_4(out_5[2]), .in_2(in_2[2]), .in_3(cpu_adder_7_out_5), .in_1(in_1[2]));
  cpu_adder cpu_adder_7 (
    .out_5(cpu_adder_7_out_5), .out_4(out_5[1]), .in_2(in_2[1]), .in_3(cpu_adder_8_out_5), .in_1(in_1[1]));
  cpu_adder cpu_adder_8 (.out_5(cpu_adder_8_out_5), .out_4(out_5[0]), .in_2(in_2[0]), .in_3(in_3), .in_1(in_1[0]));
endmodule

module cpu_shr (
  input  [7:0] in_1,
  input  in_2,
  output out_3,
  output [7:0] out_4
);

  wire [7:1] cpu_reg_8_1_out_5;

  cpu_reg_8 cpu_reg_8_1 (.out_5({cpu_reg_8_1_out_5, out_3}), .in_1(in_1), .in_2(1'b1), .in_3(1'b1));  // open: out_4
  cpu_reg_8 cpu_reg_8_2 (.out_5(out_4), .in_1({in_2, cpu_reg_8_1_out_5}), .in_2(1'b1), .in_3(1'b1));  // open: out_4
endmodule

module cpu_shl (
  input  in_1,
  input  [7:0] in_2,
  output [7:0] out_3,
  output out_4
);

  wire [6:0] cpu_reg_8_1_out_5;

  cpu_reg_8 cpu_reg_8_1 (.out_5({out_4, cpu_reg_8_1_out_5}), .in_1(in_2), .in_2(1'b1), .in_3(1'b1));  // open: out_4
  cpu_reg_8 cpu_reg_8_2 (.out_5(out_3), .in_1({cpu_reg_8_1_out_5, in_1}), .in_2(1'b1), .in_3(1'b1));  // open: out_4
endmodule

module cpu_not_8 (
  input  [7:0] in_1,
  output [7:0] out_2
);

  assign out_2 = ~in_1;  // NOT_Gate not_1, 8 bits wide
endmodule

module cpu_and_8 (
  input  [7:0] in_1,
  input  [7:0] in_2,
  output [7:0] out_3
);

  and and_1 (out_3[0], in_1[0], in_2[0]);
  and and_2 (out_3[1], in_1[1], in_2[1]);
  and and_3 (out_3[2], in_1[2], in_2[2]);
  and and_4 (out_3[3], in_1[3], in_2[3]);
  and and_5 (out_3[4], in_1[4], in_2[4]);
  and and_6 (out_3[5], in_1[5], in_2[5]);
  and and_7 (out_3[6], in_1[6], in_2[6]);
  and and_8 (out_3[7], in_1[7], in_2[7]);
endmodule

module cpu_or_8 (
  input  [7:0] in_1,
  input  [7:0] in_2,
  output [7:0] out_3
);

  or or_1 (out_3[0], in_1[0], in_2[0]);
  or or_2 (out_3[1], in_1[1], in_2[1]);
  or or_3 (out_3[2], in_1[2], in_2[2]);
  or or_4 (out_3[3], in_1[3], in_2[3]);
  or or_5 (out_3[4], in_1[4], in_2[4]);
  or or_6 (out_3[5], in_1[5], in_2[5]);
  or or_7 (out_3[6], in_1[6], in_2[6]);
  or or_8 (out_3[7], in_1[7], in_2[7]);
endmodule

module cpu_xor_le_1 (
  input  in_1,
  input  in_2,
  input  in_3,
  input  in_4,
  output out_5,
  output out_6,
  output out_7
);

  wire and_2_out, and_3_out, and_4_out, not_1_out, not_2_out, or_1_out;

  xor xor_1 (out_5, in_3, in_4);
  not not_1 (not_1_out, out_5);
  and and_1 (out_6, not_1_out, in_1);
  and and_2 (and_2_out, in_4, in_3, in_2);
  and and_3 (and_3_out, in_1, in_3, out_5);
  not not_2 (not_2_out, in_4);
  or or_1 (or_1_out, and_3_out, in_3, in_2);
  and and_4 (and_4_out, or_1_out, not_2_out);
  or or_2 (out_7, and_2_out, and_4_out);
endmodule

module cpu_xor_le_8 (
  input  [7:0] in_1,
  input  [7:0] in_2,
  output [7:0] out_3,
  output out_4,
  output out_5
);

  wire cpu_xor_le_1_1_out_6, cpu_xor_le_1_1_out_7, cpu_xor_le_1_2_out_6, cpu_xor_le_1_2_out_7,
       cpu_xor_le_1_3_out_6, cpu_xor_le_1_3_out_7, cpu_xor_le_1_4_out_6, cpu_xor_le_1_4_out_7,
       cpu_xor_le_1_5_out_6, cpu_xor_le_1_5_out_7, cpu_xor_le_1_6_out_6, cpu_xor_le_1_6_out_7,
       cpu_xor_le_1_7_out_6, cpu_xor_le_1_7_out_7;

  cpu_xor_le_1 cpu_xor_le_1_1 (
    .out_6(cpu_xor_le_1_1_out_6), .out_5(out_3[0]), .out_7(cpu_xor_le_1_1_out_7), .in_1(1'b1), .in_2(1'b0),
    .in_3(in_1[0]), .in_4(in_2[0]));
  cpu_xor_le_1 cpu_xor_le_1_2 (
    .out_6(cpu_xor_le_1_2_out_6), .out_5(out_3[1]), .out_7(cpu_xor_le_1_2_out_7),
    .in_1(cpu_xor_le_1_1_out_6), .in_2(cpu_xor_le_1_1_out_7), .in_3(in_1[1]), .in_4(in_2[1]));
  cpu_xor_le_1 cpu_xor_le_1_3 (
    .out_6(cpu_xor_le_1_3_out_6), .out_5(out_3[2]), .out_7(cpu_xor_le_1_3_out_7),
    .in_1(cpu_xor_le_1_2_out_6), .in_2(cpu_xor_le_1_2_out_7), .in_3(in_1[2]), .in_4(in_2[2]));
  cpu_xor_le_1 cpu_xor_le_1_4 (
    .out_6(cpu_xor_le_1_4_out_6), .out_5(out_3[3]), .out_7(cpu_xor_le_1_4_out_7),
    .in_1(cpu_xor_le_1_3_out_6), .in_2(cpu_xor_le_1_3_out_7), .in_3(in_1[3]), .in_4(in_2[3]));
  cpu_xor_le_1 cpu_xor_le_1_5 (
    .out_6(cpu_xor_le_1_5_out_6), .out_5(out_3[4]), .out_7(cpu_xor_le_1_5_out_7),
    .in_1(cpu_xor_le_1_4_out_6), .in_2(cpu_xor_le_1_4_out_7), .in_3(in_1[4]), .in_4(in_2[4]));
  cpu_xor_le_1 cpu_xor_le_1_6 (
    .out_6(cpu_xor_le_1_6_out_6), .out_5(out_3[5]), .out_7(cpu_xor_le_1_6_out_7),
    .in_1(cpu_xor_le_1_5_out_6), .in_2(cpu_xor_le_1_5_out_7), .in_3(in_1[5]), .in_4(in_2[5]));
  cpu_xor_le_1 cpu_xor_le_1_7 (
    .out_6(cpu_xor_le_1_7_out_6), .out_5(out_3[6]), .out_7(cpu_xor_le_1_7_out_7),
    .in_1(cpu_xor_le_1_6_out_6), .in_2(cpu_xor_le_1_6_out_7), .in_3(in_1[6]), .in_4(in_2[6]));
  cpu_xor_le_1 cpu_xor_le_1_8 (
    .out_6(out_5), .out_5(out_3[7]), .out_7(out_4), .in_1(cpu_xor_le_1_7_out_6), .in_2(cpu_xor_le_1_7_out_7),
    .in_3(in_1[7]), .in_4(in_2[7]));
endmodule

module cpu_alu (
  input  [7:0] in_1,
  input  [7:0] in_2,
  input  in_3,
  input  in_4,
  input  in_5,
  input  in_6,
  output out_7,
  output out_8,
  output out_9,
  output [7:0] out_10,
  output out_11
);

  wire and_1_out, and_2_out, and_3_out, cpu_3x8_dec_1_out_4, cpu_3x8_dec_1_out_5, cpu_3x8_dec_1_out_6,
       cpu_3x8_dec_1_out_7, cpu_3x8_dec_1_out_8, cpu_3x8_dec_1_out_9, cpu_3x8_dec_1_out_10,
       cpu_adder_8_1_out_4, cpu_shl_1_out_4, cpu_shr_1_out_3;
  wire [7:0] cpu_adder_8_1_out_5, cpu_and_8_1_out_3, cpu_not_8_1_out_2, cpu_or_8_1_out_3, cpu_shl_1_out_3,
       cpu_shr_1_out_4, cpu_xor_le_8_1_out_3;

  cpu_xor_le_8 cpu_xor_le_8_1 (.out_4(out_7), .out_5(out_8), .out_3(cpu_xor_le_8_1_out_3), .in_2(in_2), .in_1(in_1));
  cpu_or_8 cpu_or_8_1 (.out_3(cpu_or_8_1_out_3), .in_2(in_2), .in_1(in_1));
  cpu_and_8 cpu_and_8_1 (.out_3(cpu_and_8_1_out_3), .in_2(in_2), .in_1(in_1));
  cpu_not_8 cpu_not_8_1 (.out_2(cpu_not_8_1_out_2), .in_1(in_1));
  cpu_shl cpu_shl_1 (.out_4(cpu_shl_1_out_4), .out_3(cpu_shl_1_out_3), .in_2(in_1));  // open: in_1
  cpu_shr cpu_shr_1 (.out_3(cpu_shr_1_out_3), .out_4(cpu_shr_1_out_4), .in_1(in_1));  // open: in_2
  cpu_adder_8 cpu_adder_8_1 (
    .out_4(cpu_adder_8_1_out_4), .out_5(cpu_adder_8_1_out_5), .in_1(in_1), .in_2(in_2), .in_3(in_3));
  cpu_enable_8 cpu_enable_8_1 (.out_3(out_10), .in_1(cpu_xor_le_8_1_out_3), .in_2(cpu_3x8_dec_1_out_10));
  cpu_enable_8 cpu_enable_8_2 (.out_3(out_10), .in_1(cpu_or_8_1_out_3), .in_2(cpu_3x8_dec_1_out_9));
  cpu_enable_8 cpu_enable_8_3 (.out_3(out_10), .in_1(cpu_and_8_1_out_3), .in_2(cpu_3x8_dec_1_out_8));
  cpu_enable_8 cpu_enable_8_4 (.out_3(out_10), .in_1(cpu_not_8_1_out_2), .in_2(cpu_3x8_dec_1_out_7));
  cpu_enable_8 cpu_enable_8_5 (.out_3(out_10), .in_1(cpu_shl_1_out_3), .in_2(cpu_3x8_dec_1_out_6));
  cpu_enable_8 cpu_enable_8_6 (.out_3(out_10), .in_1(cpu_shr_1_out_4), .in_2(cpu_3x8_dec_1_out_5));
  cpu_enable_8 cpu_enable_8_7 (.out_3(out_10), .in_1(cpu_adder_8_1_out_5), .in_2(cpu_3x8_dec_1_out_4));
  cpu_3x8_dec cpu_3x8_dec_1 (
    .out_4(cpu_3x8_dec_1_out_4), .out_5(cpu_3x8_dec_1_out_5), .out_6(cpu_3x8_dec_1_out_6),
    .out_7(cpu_3x8_dec_1_out_7), .out_8(cpu_3x8_dec_1_out_8), .out_9(cpu_3x8_dec_1_out_9),
    .out_10(cpu_3x8_dec_1_out_10), .in_1(in_4), .in_2(in_5), .in_3(in_6));  // open: out_11
  and and_1 (and_1_out, cpu_3x8_dec_1_out_6, cpu_shl_1_out_4);
  assign out_11 = cpu_3x8_dec_1_out_6 ? and_1_out : 1'bz;  // Controlled_Buffer controlled_buffer_1
  and and_2 (and_2_out, cpu_3x8_dec_1_out_5, cpu_shr_1_out_3);
  assign out_11 = cpu_3x8_dec_1_out_5 ? and_2_out : 1'bz;  // Controlled_Buffer controlled_buffer_2
  and and_3 (and_3_out, cpu_3x8_dec_1_out_4, cpu_adder_8_1_out_4);
  assign out_11 = cpu_3x8_dec_1_out_4 ? and_3_out : 1'bz;  // Controlled_Buffer controlled_buffer_3
  cpu_alu_0 cpu_alu_0_1 (.out_2(out_9), .in_1(out_10));
endmodule

module cpu_alu_0 (
  input  [7:0] in_1,
  output out_2
);

  wire or_1_out;

  or or_1 (or_1_out, in_1[0], in_1[1], in_1[2], in_1[3], in_1[4], in_1[5], in_1[6], in_1[7]);
  not not_1 (out_2, or_1_out);
endmodule

module cpu_r (
  input  [7:0] in_1,
  input  in_2,
  input  in_3,
  output [7:0] out_4,
  output [7:0] out_5
);

  cpu_reg_8 cpu_reg_8_1 (.out_4(out_5), .out_5(out_4), .in_1(in_1), .in_2(in_2), .in_3(in_3));
endmodule

module cpu_r_tmp (
  input  [7:0] in_1,
  input  in_2,
  output [7:0] out_3
);

  wire [7:0] controlled_buffer_1_out;

  assign controlled_buffer_1_out = in_2 ? in_1 : 8'bz;  // Controlled_Buffer controlled_buffer_1
  cpu_8bit_mem cpu_8bit_mem_1 (.out_3(out_3), .in_1(controlled_buffer_1_out), .in_2(in_2));
endmodule

module cpu_bus_1 (
  input  [7:0] in_1,
  input  in_2,
  output [7:0] out_3
);

  wire not_1_out;

  and and_1 (out_3[7], in_1[7], not_1_out);
  and and_2 (out_3[6], in_1[6], not_1_out);
  and and_3 (out_3[5], in_1[5], not_1_out);
  and and_4 (out_3[4], in_1[4], not_1_out);
  and and_5 (out_3[3], in_1[3], not_1_out);
  and and_6 (out_3[2], in_1[2], not_1_out);
  and and_7 (out_3[1], in_1[1], not_1_out);
  not not_1 (not_1_out, in_2);
  or or_1 (out_3[0], in_1[0], in_2);
endmodule

module cpu_r_accum (
  input  [7:0] in_1,
  input  in_2,
  input  in_3,
  output [7:0] out_4
);

  cpu_reg_8 cpu_reg_8_1 (.out_5(out_4), .in_1(in_1), .in_2(in_2), .in_3(in_3));  // open: out_4
endmodule

module cpu_r_iar (
  input  [7:0] in_1,
  input  in_2,
  input  in_3,
  output [7:0] out_4
);

  cpu_reg_8 cpu_reg_8_1 (.out_5(out_4), .in_1(in_1), .in_2(in_2), .in_3(in_3));  // open: out_4

  // Notes on the sheet:
  //   out_4: pull=down
endmodule

module cpu_r_ir (
  input  [7:0] in_1,
  input  in_2,
  output [7:0] out_3
);

  wire [7:0] controlled_buffer_1_out;

  assign controlled_buffer_1_out = in_2 ? in_1 : 8'bz;  // Controlled_Buffer controlled_buffer_1
  cpu_8bit_mem cpu_8bit_mem_1 (.out_3(out_3), .in_1(controlled_buffer_1_out), .in_2(in_2));
endmodule

module cpu_flags (
  input  in_1,
  input  in_2,
  input  in_3,
  input  in_4,
  input  in_5,
  output out_6,
  output out_7,
  output out_8,
  output out_9
);

  cpu_1bit_mem cpu_1bit_mem_1 (.in_1(in_1), .in_2(in_5), .out_3(out_6));
  cpu_1bit_mem cpu_1bit_mem_2 (.in_1(in_2), .in_2(in_5), .out_3(out_7));
  cpu_1bit_mem cpu_1bit_mem_3 (.in_1(in_3), .in_2(in_5), .out_3(out_8));
  cpu_1bit_mem cpu_1bit_mem_4 (.in_1(in_4), .in_2(in_5), .out_3(out_9));
endmodule

module cpu_clock (
  input  in_1,
  output out_2,
  output out_3,
  output out_4
);

  wire j_k_ff_1_qn, nand_1_out;

  J_K_Flip_Flop j_k_ff_1 (.J(1'b1), .clk(in_1), .K(1'b1), .Q(out_2), .Qn(j_k_ff_1_qn));  // open: preset, reset
  nand nand_1 (nand_1_out, in_1, out_2);
  nand nand_2 (out_4, j_k_ff_1_qn, in_1);
  not not_1 (out_3, nand_1_out);
endmodule

module cpu_stepper (
  input  in_1,
  input  in_2,
  output out_3,
  output out_4,
  output out_5,
  output out_6,
  output out_7,
  output out_8,
  output out_9
);

  wire cpu_1bit_mem_1_out_3, cpu_1bit_mem_2_out_3, cpu_1bit_mem_3_out_3, cpu_1bit_mem_4_out_3,
       cpu_1bit_mem_5_out_3, cpu_1bit_mem_6_out_3, cpu_1bit_mem_7_out_3, cpu_1bit_mem_8_out_3,
       cpu_1bit_mem_9_out_3, cpu_1bit_mem_10_out_3, cpu_1bit_mem_11_out_3, not_1_out, not_2_out, not_3_out,
       not_4_out, not_5_out, not_6_out, not_7_out, not_8_out, or_1_out, or_2_out;

  not not_1 (not_1_out, in_2);
  not not_2 (not_2_out, in_1);
  or or_1 (or_1_out, in_1, in_2);
  or or_2 (or_2_out, in_1, not_1_out);
  or or_3 (out_3, in_1, not_3_out);
  cpu_1bit_mem cpu_1bit_mem_1 (.in_1(not_2_out), .in_2(or_1_out), .out_3(cpu_1bit_mem_1_out_3));
  not not_3 (not_3_out, cpu_1bit_mem_2_out_3);
  cpu_1bit_mem cpu_1bit_mem_2 (.in_1(cpu_1bit_mem_1_out_3), .in_2(or_2_out), .out_3(cpu_1bit_mem_2_out_3));
  and and_1 (out_4, cpu_1bit_mem_2_out_3, not_4_out);
  not not_4 (not_4_out, cpu_1bit_mem_4_out_3);
  cpu_1bit_mem cpu_1bit_mem_3 (.in_1(cpu_1bit_mem_2_out_3), .in_2(or_1_out), .out_3(cpu_1bit_mem_3_out_3));
  cpu_1bit_mem cpu_1bit_mem_4 (.in_1(cpu_1bit_mem_3_out_3), .in_2(or_2_out), .out_3(cpu_1bit_mem_4_out_3));
  and and_2 (out_5, cpu_1bit_mem_4_out_3, not_5_out);
  cpu_1bit_mem cpu_1bit_mem_5 (.in_1(cpu_1bit_mem_4_out_3), .in_2(or_1_out), .out_3(cpu_1bit_mem_5_out_3));
  not not_5 (not_5_out, cpu_1bit_mem_6_out_3);
  cpu_1bit_mem cpu_1bit_mem_6 (.in_1(cpu_1bit_mem_5_out_3), .in_2(or_2_out), .out_3(cpu_1bit_mem_6_out_3));
  and and_3 (out_6, cpu_1bit_mem_6_out_3, not_6_out);
  not not_6 (not_6_out, cpu_1bit_mem_8_out_3);
  cpu_1bit_mem cpu_1bit_mem_7 (.in_1(cpu_1bit_mem_6_out_3), .in_2(or_1_out), .out_3(cpu_1bit_mem_7_out_3));
  cpu_1bit_mem cpu_1bit_mem_8 (.in_1(cpu_1bit_mem_7_out_3), .in_2(or_2_out), .out_3(cpu_1bit_mem_8_out_3));
  and and_4 (out_7, cpu_1bit_mem_8_out_3, not_7_out);
  cpu_1bit_mem cpu_1bit_mem_9 (.in_1(cpu_1bit_mem_8_out_3), .in_2(or_1_out), .out_3(cpu_1bit_mem_9_out_3));
  not not_7 (not_7_out, cpu_1bit_mem_10_out_3);
  cpu_1bit_mem cpu_1bit_mem_10 (.in_1(cpu_1bit_mem_9_out_3), .in_2(or_2_out), .out_3(cpu_1bit_mem_10_out_3));
  and and_5 (out_8, cpu_1bit_mem_10_out_3, not_8_out);
  not not_8 (not_8_out, out_9);
  cpu_1bit_mem cpu_1bit_mem_11 (.in_1(cpu_1bit_mem_10_out_3), .in_2(or_1_out), .out_3(cpu_1bit_mem_11_out_3));
  cpu_1bit_mem cpu_1bit_mem_12 (.in_1(cpu_1bit_mem_11_out_3), .in_2(or_2_out), .out_3(out_9));
endmodule

module cpu_control_unit (
  input  Refresh,
  input  clks,
  input  clk,
  input  clke,
  input  [7:0] IR_IN,
  output out_6,
  output MAR_S,
  output RAM_E,
  output ACC_S,
  output ACC_E,
  output RAM_S,
  output IAR_E,
  output TMP_S,
  output R0_S,
  output R0_E,
  output R1_S,
  output R1_E,
  output R2_S,
  output R2_E,
  output R3_S,
  output R3_E,
  output IR_S,
  output IAR_S
);

  wire cpu_stepper_1_out_4, cpu_stepper_1_out_5, cpu_stepper_1_out_6, cpu_stepper_1_out_7,
       cpu_stepper_1_out_8, cpu_stepper_1_out_9, or_1_out;

  and and_1 (RAM_E, clke, cpu_stepper_1_out_4);
  and and_2 (ACC_E, clke, cpu_stepper_1_out_5);
  and and_3 (IAR_E, clke, out_6);
  and and_4 (R0_E, clke, 1'b0);
  and and_5 (R1_E, clke, 1'b0);
  and and_6 (R2_E, clke, 1'b0);
  and and_7 (R3_E, clke, 1'b0);
  cpu_stepper cpu_stepper_1 (
    .out_8(cpu_stepper_1_out_8), .out_9(cpu_stepper_1_out_9), .out_3(out_6), .out_4(cpu_stepper_1_out_4),
    .out_5(cpu_stepper_1_out_5), .out_6(cpu_stepper_1_out_6), .out_7(cpu_stepper_1_out_7), .in_1(or_1_out),
    .in_2(clk));
  or or_1 (or_1_out, Refresh, cpu_stepper_1_out_9);
  and and_8 (MAR_S, clks, out_6);
  and and_9 (ACC_S, clks, out_6);
  and and_10 (RAM_S, clks, 1'b0);
  and and_11 (TMP_S, clks, 1'b0);
  and and_12 (R0_S, clks, 1'b0);
  and and_13 (R1_S, clks, 1'b0);
  and and_14 (R2_S, clks, 1'b0);
  and and_15 (R3_S, clks, 1'b0);
  and and_16 (IR_S, clks, cpu_stepper_1_out_4);
  and and_17 (IAR_S, clks, cpu_stepper_1_out_5);
endmodule
